// Logisim project 1l.circ as structural Verilog: 2 circuits, main circuit main
module main (
  input  a,
  input  b,
  input  c_in,
  output S,
  output C_out
);

  wire not_1_out, not_2_out, not_3_out, or_1_out, or_2_out, or_3_out, or_4_out, or_5_out, or_6_out, or_7_out;

  not not_1 (not_1_out, a);
  not not_2 (not_2_out, b);
  not not_3 (not_3_out, c_in);
  or or_1 (or_1_out, a, b);
  or or_2 (or_2_out, a, c_in);
  or or_3 (or_3_out, b, c_in);
  or or_4 (or_4_out, a, b, c_in);
  or or_5 (or_5_out, a, not_2_out, not_3_out);
  or or_6 (or_6_out, b, not_1_out, not_3_out);
  or or_7 (or_7_out, c_in, not_1_out, not_2_out);
  and and_1 (C_out, or_1_out, or_2_out, or_3_out);
  and and_2 (S, or_4_out, or_5_out, or_6_out, or_7_out);
endmodule

module adder8 (
  input  in_1,
  input  in_2,
  input  in_3,
  input  in_4,
  input  in_5,
  input  in_6,
  input  in_7,
  input  in_8,
  input  in_9,
  input  in_10,
  input  in_11,
  input  in_12,
  input  in_13,
  input  in_14,
  input  in_15,
  input  in_16,
  output S0,
  output S1,
  output S2,
  output S3,
  output S4,
  output S5,
  output S6,
  output S7,
  output C8
);

  wire main_1_c_out, main_2_c_out, main_3_c_out, main_4_c_out, main_5_c_out, main_6_c_out, main_7_c_out;

  main main_1 (.a(in_1), .b(in_2), .c_in(1'b0), .S(S0), .C_out(main_1_c_out));
  main main_2 (.a(in_3), .b(in_4), .c_in(main_1_c_out), .S(S1), .C_out(main_2_c_out));
  main main_3 (.a(in_5), .b(in_6), .c_in(main_2_c_out), .S(S2), .C_out(main_3_c_out));
  main main_4 (.a(in_7), .b(in_8), .c_in(main_3_c_out), .S(S3), .C_out(main_4_c_out));
  main main_5 (.a(in_9), .b(in_10), .c_in(main_4_c_out), .S(S4), .C_out(main_5_c_out));
  main main_6 (.a(in_11), .b(in_12), .c_in(main_5_c_out), .S(S5), .C_out(main_6_c_out));
  main main_7 (.a(in_13), .b(in_14), .c_in(main_6_c_out), .S(S6), .C_out(main_7_c_out));
  main main_8 (.a(in_15), .b(in_16), .c_in(main_7_c_out), .S(S7), .C_out(C8));
endmodule
