// Logisim project counter8_T.circ as structural Verilog: 1 circuit, main circuit Counter8
module Counter8 (
  output Q2,
  output Q1,
  output Q0
);

  wire and_1_out, CLK_out;

  and and_1 (and_1_out, Q0, Q1);
  Clock CLK (.out(CLK_out));
  T_Flip_Flop FF2 (.T(and_1_out), .clk(CLK_out), .Q(Q2));  // open: Qn, reset, preset
  T_Flip_Flop FF1 (.T(Q0), .clk(CLK_out), .Q(Q1));  // open: Qn, reset, preset
  T_Flip_Flop FF0 (.T(1'b1), .clk(CLK_out), .Q(Q0));  // open: Qn, reset, preset
endmodule
