// Logisim project gray_bcd_plus1.circ as structural Verilog: 3 circuits, main circuit Main
module Main (
  input  in_1,
  input  in_2,
  input  in_3,
  input  in_4,
  input  in_5,
  input  in_6,
  input  in_7,
  input  in_8,
  output G4,
  output out_10,
  output out_11,
  output out_12,
  output out_13
);

  wire [3:0] adder_1_out, adder_2_out, gray_1_o0, gray_2_o0;
  wire [4:4] adder_1_cout;

  Gray gray_1 (
    .I3(in_1), .I2(in_2), .I1(in_3), .I0(in_4), .O3(gray_1_o0[3]), .O2(gray_1_o0[2]), .O1(gray_1_o0[1]),
    .O0(gray_1_o0[0]));
  Gray gray_2 (
    .I3(in_5), .I2(in_6), .I1(in_7), .I0(in_8), .O3(gray_2_o0[3]), .O2(gray_2_o0[2]), .O1(gray_2_o0[1]),
    .O0(gray_2_o0[0]));
  Adder #(.width(4)) adder_1 (.a(gray_1_o0), .b(gray_2_o0), .out(adder_1_out), .cout(adder_1_cout[4]));  // open: cin
  Adder #(.width(5)) adder_2 (
    .a({adder_1_cout[4], adder_1_out}), .b(5'b00001), .out({G4, adder_2_out}));  // open: cin, cout
  xor xor_1 (out_10, G4, adder_2_out[3]);
  xor xor_2 (out_11, adder_2_out[3], adder_2_out[2]);
  xor xor_3 (out_12, adder_2_out[2], adder_2_out[1]);
  xor xor_4 (out_13, adder_2_out[1], adder_2_out[0]);
endmodule

module Gray (
  input  I3,
  input  I2,
  input  I1,
  input  I0,
  output O3,
  output O2,
  output O1,
  output O0
);

  wire and_1_out, and_2_out, and_3_out, and_4_out, and_5_out, and_6_out, and_7_out, and_8_out, and_9_out,
       and_10_out, not_1_out, not_2_out, not_3_out, not_4_out, not_6_out, not_7_out, not_8_out, not_9_out,
       not_10_out;

  and and_1 (and_1_out, I3, I0);
  and and_2 (and_2_out, I3, I1);
  not not_1 (not_1_out, I1);
  and and_3 (and_3_out, not_1_out, not_2_out);
  not not_2 (not_2_out, I0);
  not not_3 (not_3_out, I3);
  and and_4 (and_4_out, not_3_out, I2, I0);
  and and_5 (and_5_out, I3, not_4_out);
  not not_4 (not_4_out, I0);
  not not_5 (O1, I0);
  not not_6 (not_6_out, I2);
  not not_7 (not_7_out, I3);
  not not_8 (not_8_out, I1);
  not not_9 (not_9_out, I0);
  not not_10 (not_10_out, I0);
  or or_1 (O3, and_1_out, and_2_out);
  or or_2 (O2, and_3_out, and_4_out, and_5_out);
  and and_6 (and_6_out, not_6_out, I1, I0);
  and and_7 (and_7_out, not_7_out, I2, not_8_out, I0);
  and and_8 (and_8_out, I2, I1, not_9_out);
  and and_9 (and_9_out, I3, not_10_out);
  and and_10 (and_10_out, I3, I1);
  or or_3 (O0, and_6_out, and_7_out, and_8_out, and_9_out, and_10_out);
endmodule

module enc_to_Gray (
  input  B4,
  input  B3,
  input  B2,
  input  B1,
  input  B0,
  output G3,
  output G3_2,
  output G2,
  output G1,
  output G0
);

  xor xor_1 (G3_2, B4, B3);
  xor xor_2 (G2, B3, B2);
  xor xor_3 (G1, B2, B1);
  xor xor_4 (G0, B1, B0);

  assign G3 = B4;
endmodule
